// Logisim project kim_fp_part1.circ as structural Verilog: 4 circuits, main circuit 8-Bit Calculator
module main (
  input  in_1,
  input  in_2,
  input  in_3,
  input  in_4,
  input  in_5,
  input  in_6,
  input  in_7,
  input  in_8
);

  wire button_5_out;
  wire [3:0] button_out, n8_bit_calculator_1_display_3_0, n8_bit_calculator_1_display_7_4;

  Hex_Digit_Display hex_digit_display_1 (.value(n8_bit_calculator_1_display_3_0));  // open: dp
  Hex_Digit_Display hex_digit_display_2 (.value(n8_bit_calculator_1_display_7_4));  // open: dp
  _8_Bit_Calculator u_8_bit_calculator_1 (
    .Display_7_4(n8_bit_calculator_1_display_7_4), .Display_3_0(n8_bit_calculator_1_display_3_0),
    .in_3(in_1), .in_4(in_2), .in_5(in_3), .in_6(in_4), .in_7(in_5), .in_8(in_6), .in_9(in_7), .in_10(in_8),
    .Operator(button_out), .Equals(button_5_out));
  Button button (.out(button_out[0]));
  Button button_2 (.out(button_out[1]));
  Button button_3 (.out(button_out[2]));
  Button button_4 (.out(button_out[3]));
  Button button_5 (.out(button_5_out));
endmodule

module _8_Bit_Calculator (
  input  [3:0] Operator,
  input  Equals,
  input  in_3,
  input  in_4,
  input  in_5,
  input  in_6,
  input  in_7,
  input  in_8,
  input  in_9,
  input  in_10,
  output [3:0] Display_7_4,
  output [3:0] Display_3_0
);

  Datapath__FP_Part_2 Datapath (
    .Data_Out({Display_7_4, Display_3_0}), .Data_In({in_3, in_4, in_5, in_6, in_7, in_8, in_9, in_10}));
  Controller__FP_Part_1 Controller ();  // open: ø, e
endmodule

module Controller__FP_Part_1 (
  input  [3:0] \ø ,
  input  e
);

  wire clock_1_out, not_1_out, not_2_out, not_3_out, not_4_out, not_5_out, not_6_out, not_7_out, or_1_out,
       or_2_out;

  not not_1 (not_1_out, \ø [0]);
  not not_2 (not_2_out, \ø [1]);
  not not_3 (not_3_out, \ø [2]);
  not not_4 (not_4_out, \ø [3]);
  or or_1 (or_1_out, \ø [0], \ø [1], \ø [2], \ø [3]);
  // AND_Gate and_1 has open pins: in0=or_1_out, in1=not_5_out, out=open
  not not_5 (not_5_out, e);
  not not_6 (not_6_out, or_2_out);
  or or_2 (or_2_out, \ø [0], \ø [1], \ø [2], \ø [3]);
  // AND_Gate and_2 has open pins: in0=not_6_out, in1=not_7_out, out=open
  not not_7 (not_7_out, e);
  // AND_Gate and_3 has open pins: in0=not_1_out, in1=not_2_out, in2=not_3_out, in3=not_4_out, in4=e, out=open
  Register #(.width(1)) x (.clk(clock_1_out));  // open: D, en, Q, clr
  Register #(.width(1)) y (.clk(clock_1_out));  // open: D, en, Q, clr
  Clock clock_1 (.out(clock_1_out));
endmodule

module Datapath__FP_Part_2 (
  input  [7:0] Data_In,
  output [7:0] Data_Out
);
endmodule
